# Fritzing sketch A500-Mitsumi-v1.0 (saved by Fritzing 1.0.2b)
circuit board: 16.8cm x 3.94998cm
breadboards: 1

parts:
  6570-036 = IC, DIP package, 40 pins [chip_label=IC]
  LS27 = IC, DIP package, 14 pins [chip_label=IC]
  LS123 = IC, DIP package, 16 pins [chip_label=IC]
  NE555 = IC, DIP package, 8 pins [chip_label=IC]
  Amiga_Connector = female pin header, 8 pins [form="♀ (female)"]
  Floppy_LED = female pin header, 2 pins [form="♀ (female)"]
  Amiga_Connector5 = female pin header, 2 pins [form="♀ (female)"]
  Amiga_Connector6 = female pin header, 2 pins [form="♀ (female)"]
  Power_LED = female pin header, 2 pins [form="♀ (female)"]
  3MHz = Crystal [frequency="16 Mhz" package=THT]
  10pF = Ceramic Capacitor [capacitance=100nF voltage=35V package="200 mil [THT, multilayer]"]
  10pF_2 = Ceramic Capacitor [capacitance=100nF voltage=35V package="200 mil [THT, multilayer]"]
  100nF = Ceramic Capacitor [capacitance=100nF voltage=35V package="200 mil [THT, multilayer]"]
  1nF = Ceramic Capacitor [capacitance=100nF voltage=35V package="200 mil [THT, multilayer]"]
  1nF_2 = Ceramic Capacitor [capacitance=100nF voltage=35V package="200 mil [THT, multilayer]"]
  2SC458 = TRANSISTOR_NPN [package=to-92-ammo]
  150 = Resistor [tolerance=±5% power=0.25W resistance=220 package=THT]
  100 = Resistor [tolerance=±5% power=0.25W resistance=220 package=THT]
  22µF = Capacitor Polarized [package=cpol-radial-10uf-25v]
  2SC458_2 = TRANSISTOR_NPN [package=to-92-ammo]
  47K = Resistor [tolerance=±5% power=0.25W resistance=220 package=THT]
  47K_2 = Resistor [tolerance=±5% power=0.25W resistance=220 package=THT]
  10µF = Capacitor Polarized [package=cpol-radial-10uf-25v]
  100nF_2 = Ceramic Capacitor [capacitance=100nF voltage=35V package="200 mil [THT, multilayer]"]
  1µF = Capacitor Polarized [package=cpol-radial-10uf-25v]
  120K = Resistor [tolerance=±5% power=0.25W resistance=220 package=THT]
  1M = Resistor [tolerance=±5% power=0.25W resistance=220 package=THT]
  100nF_3 = Ceramic Capacitor [capacitance=100nF voltage=35V package="200 mil [THT, multilayer]"]
  100nF_4 = Ceramic Capacitor [capacitance=100nF voltage=35V package="200 mil [THT, multilayer]"]
  22 = Resistor [tolerance=±5% power=0.25W resistance=220 package=THT]
  22_2 = Resistor [tolerance=±5% power=0.25W resistance=220 package=THT]
  10K = Resistor [tolerance=±5% power=0.25W resistance=220 package=THT]
  100nF_5 = Ceramic Capacitor [capacitance=100nF voltage=35V package="200 mil [THT, multilayer]"]
  47K_3 = Resistor [tolerance=±5% power=0.25W resistance=220 package=THT]
  100nF_6 = Ceramic Capacitor [capacitance=100nF voltage=35V package="200 mil [THT, multilayer]"]
  Amiga_Connector1 = female pin header, 15 pins [form="♀ (female)"]
  Molex_Connector_39532314 = female pin header, 16 pins [form="♀ (female)"]

nets:
  N1: 6570-036.pin1, 6570-036.pin30, 6570-036.pin40, LS27.pin14, LS123.pin2, LS123.pin3, LS123.pin10, LS123.pin11, LS123.pin16, NE555.pin4, NE555.pin8, Amiga_Connector.pin5, 100nF.1, 22µF.+, 47K.Pin_1, 47K_2.Pin_0, 100nF_2.1, 120K.Pin_1, 1M.Pin_0, 10K.Pin_1, 100nF_5.1, 47K_3.Pin_1, Molex_Connector_39532314.pin12
  N2: 6570-036.pin2, LS123.pin1, 47K_3.Pin_0
  N3: 6570-036.pin3, Molex_Connector_39532314.pin9
  N4: 6570-036.pin4, Amiga_Connector1.pin8
  N5: 6570-036.pin5, Molex_Connector_39532314.pin8
  N6: 6570-036.pin6, Amiga_Connector1.pin7
  N7: 6570-036.pin7, Molex_Connector_39532314.pin7
  N8: 6570-036.pin8, Amiga_Connector1.pin6
  N9: 6570-036.pin9, Molex_Connector_39532314.pin6
  N10: 6570-036.pin10, 3MHz.pin_0, 10pF_2.1
  N11: 6570-036.pin11, 3MHz.pin_1, 10pF.1
  N12: 6570-036.pin12, 6570-036.pin21, LS27.pin7, LS123.pin8, NE555.pin1, Amiga_Connector.pin3, Amiga_Connector5.pin1, Amiga_Connector6.pin1, 10pF.0, 10pF_2.0, 100nF.0, 1nF.0, 1nF_2.0, 2SC458.E, 22µF.-, 2SC458_2.E, 10µF.-, 100nF_2.0, 100nF_3.1, 100nF_4.0, 100nF_5.0, Amiga_Connector1.pin1
  N13: 6570-036.pin13, Amiga_Connector1.pin5
  N14: 6570-036.pin14, Molex_Connector_39532314.pin5
  N15: 6570-036.pin15, Amiga_Connector1.pin4
  N16: 6570-036.pin16, Molex_Connector_39532314.pin4
  N17: 6570-036.pin17, Amiga_Connector1.pin3
  N18: 6570-036.pin18, Molex_Connector_39532314.pin3
  N19: 6570-036.pin19, Amiga_Connector1.pin2
  N20: 6570-036.pin20, Molex_Connector_39532314.pin2
  N21: 6570-036.pin22, 100.Pin_1
  N22: 6570-036.pin23, LS27.pin3, Amiga_Connector1.pin9
  N23: 6570-036.pin24, Molex_Connector_39532314.pin10
  N24: 6570-036.pin25, Amiga_Connector1.pin10
  N25: 6570-036.pin26, LS27.pin4, Molex_Connector_39532314.pin11
  N26: 6570-036.pin27, LS27.pin5, Amiga_Connector1.pin11
  N27: 6570-036.pin28, Amiga_Connector1.pin12
  N28: 6570-036.pin29, Amiga_Connector1.pin13
  N29: 6570-036.pin31, Amiga_Connector1.pin14
  N30: 6570-036.pin32, Molex_Connector_39532314.pin15
  N31: 6570-036.pin33, Amiga_Connector1.pin15
  N32: 6570-036.pin34, Molex_Connector_39532314.pin16
  N33: 6570-036.pin35, Molex_Connector_39532314.pin14
  N34: 6570-036.pin36, Molex_Connector_39532314.pin13
  N35: 6570-036.pin37, Amiga_Connector.pin8, 1nF.1
  N36: 6570-036.pin38, Amiga_Connector.pin7, 1nF_2.1
  N37: 6570-036.pin39, LS27.pin12
  N38: LS27.pin1, LS27.pin2, LS27.pin9, LS27.pin10, LS27.pin11, NE555.pin3
  N39: LS27.pin6, 2SC458_2.C, 47K.Pin_0
  N40: LS27.pin8, Amiga_Connector.pin6
  N41: LS27.pin13, LS123.pin5
  N42: LS123.pin6, 100nF_6.0
  N43: LS123.pin7, 10K.Pin_0, 100nF_6.1
  N44: LS123.pin9, LS123.pin13
  N45: LS123.pin14, 1µF.-
  N46: LS123.pin15, 1µF.+, 120K.Pin_0
  N47: NE555.pin2, 2SC458_2.B, 1M.Pin_1, 100nF_4.1
  N48: NE555.pin5, 100nF_3.0
  N49: NE555.pin6, NE555.pin7, 47K_2.Pin_1, 10µF.+
  N50: Amiga_Connector.pin1, 22.Pin_1
  N51: Amiga_Connector.pin2, 22_2.Pin_1
  N52: Floppy_LED.pin1, Amiga_Connector5.pin2
  N53: Floppy_LED.pin2, 22.Pin_0
  N54: Amiga_Connector6.pin2, Power_LED.pin1
  N55: Power_LED.pin2, 22_2.Pin_0
  N56: 2SC458.B, 150.Pin_1
  N57: 2SC458.C, 100.Pin_0
  N58: 150.Pin_0, Molex_Connector_39532314.pin1

notes:
  16V
  50V
  Amiga 500 - Mitsumi Keyboard Controller Replica V1.0
  Reverse Engineered by Emanuele Laface
  1
  8
